# Fritzing sketch HbridgeBreakoutBoard (saved by Fritzing 0.7.10b)
breadboards: 4

parts:
  R_IH2 = Resistor [tolerance=±5% resistance=1k package=THT]
  R_IH1 = Resistor [tolerance=±5% resistance=1k package=THT]
  R_IL2 = Resistor [tolerance=±5% resistance=1k package=THT]
  R_IL1 = Resistor [tolerance=±5% resistance=1k package=THT]
  External_power_supply_connector = female pin header, 4 pins [form="♀ (female)"]
  LED_IL1 = LED - 5mm [color="Red (633nm)" package="5 mm [THT]"]
  LED_IL2 = LED - 5mm [color="Red (633nm)" package="5 mm [THT]"]
  LED_IH1 = LED - 5mm [color="Red (633nm)" package="5 mm [THT]"]
  LED_IH2 = LED - 5mm [color="Red (633nm)" package="5 mm [THT]"]
  R_LED_IL1 = Resistor [tolerance=±20% resistance=2.2k package=THT]
  R_LED_IL2 = Resistor [tolerance=±20% resistance=2.2k package=THT]
  R_LED_IH1 = Resistor [tolerance=±20% resistance=2.2k package=THT]
  R_LED_IH2 = Resistor [tolerance=±20% resistance=2.2k package=THT]
  Arduino_connector = female pin header, 5 pins [form="♀ (female)"]
  J4 = male pin header, 2 pins [form="♂ (male)"]
  LED_TEST_A = LED - 5mm [color="Red (633nm)" package="5 mm [THT]"]
  LED_TEST_B = LED - 5mm [color="Red (633nm)" package="5 mm [THT]"]
  R_LEDS_TEST = Resistor [tolerance=±5% resistance=220 package=THT]
  J_TEST = female pin header, 2 pins [form="♀ (female)"]
  Chip_backside = female pin header, 3 pins [form="♀ (female)"]
  Chip_connector = female pin header, 15 pins [form="♀ (female)"]

nets:
  N1: R_IH2.Pin_0, LED_IH2.cathode, Arduino_connector.pin4, Chip_connector.pin10
  N2: R_IH2.Pin_1, R_IH1.Pin_1, R_IL2.Pin_1, R_IL1.Pin_1, External_power_supply_connector.pin2, R_LED_IL1.Pin_1, R_LED_IL2.Pin_1, R_LED_IH1.Pin_1, R_LED_IH2.Pin_1, J4.pin2, Chip_connector.pin3, Chip_connector.pin6, Chip_connector.pin15
  N3: R_IH1.Pin_0, LED_IH1.cathode, Arduino_connector.pin3, Chip_connector.pin7
  N4: R_IL2.Pin_0, LED_IL2.cathode, Arduino_connector.pin2, Chip_connector.pin13
  N5: R_IL1.Pin_0, LED_IL1.cathode, Arduino_connector.pin1, Chip_connector.pin1
  N6: External_power_supply_connector.pin1, Chip_backside.pin2, Chip_connector.pin8
  N7: External_power_supply_connector.pin3, Chip_backside.pin3, Chip_connector.pin5
  N8: External_power_supply_connector.pin4, Chip_backside.pin1, Chip_connector.pin11
  N9: LED_IL1.anode, R_LED_IL1.Pin_0
  N10: LED_IL2.anode, R_LED_IL2.Pin_0
  N11: LED_IH1.anode, R_LED_IH1.Pin_0
  N12: LED_IH2.anode, R_LED_IH2.Pin_0
  N13: Arduino_connector.pin5, J4.pin1
  N14: LED_TEST_A.cathode, LED_TEST_B.anode, R_LEDS_TEST.Pin_1
  N15: LED_TEST_A.anode, LED_TEST_B.cathode, J_TEST.pin1
  N16: R_LEDS_TEST.Pin_0, J_TEST.pin2

notes:
  1. 1: IL1
  2. 2: IL2
  3. 3: IH1
  4. 4: IH2
  5. GND
  +-V_high -+
  | |
  IH1 IH2
  | |
  +---M-----+
  | |
  IL1 IL2
  | |
  +-V_low---+
  Connection to chip
  Ports of chip
  Connection to Arduino
  External current
  1: external power source A
  2: external power source B
  3: load pin A
  4: load pin B
  This jumper can be used to connect the Arduino
  ground to the external power supply its ground
  Debugging board:
  - Use an Arduino 5V as the power supply
  - Connect this board as the load
  If the H bridge works, the LEDs will alternate
