# Fritzing sketch OpenerPcr (saved by Fritzing 0.8.0b)
breadboards: 5

parts:
  LCD = LCD screen
  Peltier = Peltier Element
  Thermistor = Temperature Sensor (Thermistor) [thermistor_type=NTC package=THT]
  R_Therm_1 = Resistor [tolerance=±5% resistance=220 package=THT]
  R_Therm_2 = Resistor [tolerance=±5% resistance=220 package=THT]
  External_power_supply = Power plug [part_number="Power supply"]
  External_power_supply_connector1 = female pin header, 4 pins [form="♀ (female)"]
  H_bridge_Control = female pin header, 5 pins [form="♀ (female)"]
  Arduino1 = Arduino
  Thermistor_connector = female pin header, 3 pins [form="♀ (female)"]
  R1 = Rotary Potentiometer (Small) [maximum_resistance=100kΩ]
  Connector_relays = female pin header, 3 pins [form="♀ (female)"]

nets:
  VSS: LCD.VSS, LCD.R/W, R_Therm_2.Pin_0, H_bridge_Control.pin5, Arduino1.GND, Thermistor_connector.pin2, R1.leg2, Connector_relays.pin3
  VDD: LCD.VDD, R_Therm_1.Pin_0, Arduino1.+5V, Thermistor_connector.pin1, R1.leg1, Connector_relays.pin1
  N1: LCD.V0, R1.wiper
  N2: LCD.RS, Arduino1.D8
  N3: LCD.E, Arduino1.D9
  N4: LCD.DB4, Arduino1.D10
  N5: LCD.DB5, Arduino1.D11
  N6: LCD.DB6, Arduino1.D12
  N7: LCD.DB7, Arduino1.D13
  N8: Peltier.pin1, External_power_supply_connector1.pin3
  N9: Peltier.pin2, External_power_supply_connector1.pin4
  N10: Thermistor.pin_0, Arduino1.A0, Thermistor_connector.pin3
  N11: Thermistor.pin_1, R_Therm_1.Pin_1, R_Therm_2.Pin_1
  N12: External_power_supply.GND, External_power_supply_connector1.pin2
  N13: External_power_supply.VCC, External_power_supply_connector1.pin1
  N14: H_bridge_Control.pin1, Arduino1.D2, Connector_relays.pin2
  N15: H_bridge_Control.pin2, Arduino1.D3
  N16: H_bridge_Control.pin3, Arduino1.D4
  N17: H_bridge_Control.pin4, Arduino1.D5

notes:
  H bridge breakout board
  External power
  Thermistor board
  1: 5V
  2: GND
  3: Output of thermistor [0,5] V
  Our external power supply
  H bridge breakout board
  Control
  1: external power source A
  2: external power source B
  3: load pin A
  4: load pin B
  1. 1: IL1
  2. 2: IL2
  3. 3: IH1
  4. 4: IH2
  5. GND
  Power and ground
  1. 5 V
  2. 1: IL1 (switches both relays)
  3. GND
  Relay board
  1
  OpenerPCR v.1.0
  DIY Bio Groningen
  by assert, 2014-01-24
