# Fritzing sketch OpenerPcrTask1 (saved by Fritzing 0.7.10b)
breadboards: 1

parts:
  Arduino1 = Arduino
  T2 = Temperature Sensor (Thermistor) [thermistor_type=NTC package=THT]
  R1 = Resistor [tolerance=±5% resistance=220 package=THT]
  R2 = Resistor [tolerance=±5% resistance=220 package=THT]

nets:
  N1: Arduino1.D2, T2.pin_0
  N2: Arduino1.+5V, R1.Pin_0
  N3: Arduino1.GND, R2.Pin_1
  N4: T2.pin_1, R1.Pin_1, R2.Pin_0

notes:
  - Which values does the Arduino pin read
  at which temperature?
  - Which resitor values give the highest resolution/accuracy?
  - Write an Arduino function that returns the temperature measured by the thermistor:
  double ThermistorToTemperatur(const int pin)
  {
  const int value = analogRead(pin);
  //The magic here
  const double temperature = /* ? */;
  assert(temperature >= 0.0 && "Temperature is above zero degrees Celsius);
  assert(temperature <= 110.0 && "Temperature is below 110 degrees Celsius);
  return temperature;
  }
