# Fritzing sketch OpenerPcrTask2 (saved by Fritzing 0.7.10b)
breadboards: 1

parts:
  Arduino1 = Arduino
  K1 = Relay [part_number=FRS1B-S package=THT]
  R5 = Resistor [tolerance=±5% resistance=0 part_number="Heating element" package=THT]
  R6 = Resistor [tolerance=±5% resistance=220 package=THT]
  LED1 = LED - 5mm [color="Red (633nm)" package="5 mm [THT]"]
  MIC1 = Microphone

nets:
  N1: Arduino1.GND, R5.Pin_1, R6.Pin_1, MIC1.pin2
  N2: Arduino1.D2, K1.COIL2, MIC1.pin1
  N3: Arduino1.+5V, K1.B
  N4: K1.A, LED1.anode
  N5: K1.COIL1, R6.Pin_0
  N6: K1.C1, K1.C2
  N7: R5.Pin_0, LED1.cathode

notes:
  I read that relays need
  rectifier diodes.
  Is this so (Google)? If yes, add it to the schematic
  This should be a multimeter, set to
  10 VDC
  When the frequency increases, the voltage might increase! This might damage the Arduino. Stop increasing the frequency when you notice this!
  The LED will burn if the relay is closed due to current from Arduino pin 2
  I believe the resisor should have 220 ohm, but try yourself: if the LED becomes hot, increase the resistance :)
  The relay switching port must be connected to ground with a resistance (otherwise it will short-circuit). Try to find the resistance with the highest possible value that yields reliable switching
  #include <assert.h>
  const int pin = 2; // digital pin number 2
  void setup()
  {
  setPin(pin,OUTPUT)
  }
  void loop()
  {
  const double frequency = 1.0; //Change this
  assert(frequency != 0.0);
  const double period = 1.0 / frequency;
  digitalWrite(pin,HIGH);
  delay(period);
  digitalWrite(pin,LOW);
  delay(period);
  }
  OpenPCR task 2: find out the maximum switching frequency of the relay
