# Fritzing sketch OpenerPcrTask3 (saved by Fritzing 0.7.10b)
breadboards: 1

parts:
  J1 = Peltier Element
  R1 = Resistor [tolerance=±5% resistance=220 package=THT]
  J2 = shrouded pin header, 20 pins [form="♂ (shrouded male)"]

nets:
  N1: J1.pin1, J2.pin10
  N2: J1.pin2, R1.Pin_0
  N3: R1.Pin_1, J2.pin18
  N4: J2.pin16, J2.pin17

notes:
  External power supply
  Pin bottom left = +12 VDC
  Pin top left = GND
  Check this!
  The orange connection will make the fan turn (upper pin = PS_ON, lower pin = GND)
  Which resistor to use here?
  We do have larger resistors to cope with higher currents.
  Which resistor will hold?
  Which side of the Peltier element will heat up or cool in this setup?
  The wires might get hot. How to prevent these from melting?
