# Fritzing sketch OpenerPcrTask4 (saved by Fritzing 0.7.10b)
breadboards: 1

parts:
  K4 = Relay [part_number=FRS1B-S package=THT]
  K5 = Relay [part_number=FRS1B-S package=THT]
  Arduino2 = Arduino
  LED1 = LED - 5mm [color="Red (633nm)" package="5 mm [THT]"]
  LED2 = LED - 5mm [color="Green (565nm)" package="5 mm [THT]"]
  K6 = Relay [part_number=FRS1B-S package=THT]
  R1 = Resistor [tolerance=±5% resistance=220 package=THT]
  K7 = Relay [part_number=FRS1B-S package=THT]
  R2 = Resistor [tolerance=±5% resistance=220 package=THT]

nets:
  N1: K4.A, K5.A, R1.Pin_0
  N2: K4.COIL1, K5.COIL1, K6.COIL1, K7.COIL1, R2.Pin_0
  N3: K4.C1, K4.C2
  N4: K4.COIL2, Arduino2.D2, K7.COIL2
  N5: K4.B, Arduino2.GND, K6.A, R2.Pin_1
  N6: K5.C1, K5.C2
  N7: K5.COIL2, Arduino2.D3, K6.COIL2
  N8: K5.B, Arduino2.+5V, K7.A
  N9: LED1.cathode, LED2.anode, R1.Pin_1
  N10: LED1.anode, LED2.cathode, K6.B, K7.B
  N11: K6.C1, K6.C2
  N12: K7.C1, K7.C2

notes:
  This is an H bridge. It allows to change the current direction.
  There is always at most one signal: from the yellow signal cables, from the green signal wires, or none. If pin 3 (yellow) is high, the red/green LED will burn. If pin 2 (green) is high, the green/red LED will burn. Current will always go through the resistor next to the LED. The two signals share a common resistor to ground
  Does it work?
  Use the same resistor used in series with an LED in other tasks
  Use the same resistor used in series with a relay in other tasks
  Use the same switching frequency determined in another task
  Write a class for the H bridge:
  enum HbrigeState { direction_a, direction_b, no_current };
  struct Hbridge
  {
  Hbridge(
  const HBridgeState initial_state,
  const int pin_direction_a,
  const int pin_direction_b)
  : m_pin_direction_a(pin_direction_a),
  m_pin_direction_b(pin_direction_b),
  m_state_current(initial_state),
  m_state_next(initial_state),
  {
  }
  void ToDirectionA()
  {
  //Go via state no current
  //MAGIC
  }
  void ToDirectionB()
  {
  //Go via state no current
  //MAGIC
  }
  void ToggleDirection()
  {
  //Nothing will happen is currently state is no current
  //MAGIC
  }
  void ToNoCurrent()
  {
  digitalWrite(m_pin_direction_a,LOW);
  digitalWrite(m_pin_direction_b,LOW);
  }
  private:
  static const double m_frequency = /* determined in other task */; //Hz
  const int m_pin_direction_a;
  const int m_pin_direction_b;
  HbridgeState m_state_current;
  HbridgeState m_state_next;
  };
