# Fritzing sketch OpenerPcrTask6 (saved by Fritzing 0.7.10b)
breadboards: 1

parts:
  R1 = Resistor [tolerance=±5% resistance=220 package=THT]
  J2 = shrouded pin header, 20 pins [form="♂ (shrouded male)"]
  C1 = Ceramic Capacitor [capacitance=100nF package="100 mil [THT, multilayer]"]

nets:
  N1: R1.Pin_0, C1.1
  N2: R1.Pin_1, J2.pin18
  N3: J2.pin10, C1.0
  N4: J2.pin16, J2.pin17

notes:
  External power supply
  Pin bottom left = +12 VDC
  Pin top left = GND
  Check this!
  The orange connection will make the fan turn (upper pin = PS_ON, lower pin = GND)
  Which resistor to use here?
  We do have larger resistors to cope with higher currents.
  Which resistor will hold?
  I use this capacitor symbol as a heating element :)
  The wires might get hot. How to prevent these from melting?
