# Fritzing sketch TripleAndPortCmos4073 (saved by Fritzing 0.7.10b)
breadboards: 1

parts:
  Arduino1 = Arduino
  R1 = Resistor [tolerance=±5% resistance=10k package=THT]
  R3 = Resistor [tolerance=±5% resistance=10k package=THT]
  R4 = Resistor [tolerance=±5% resistance=10k package=THT]
  LED1 = LED - 5mm [color="Red (633nm)" package="5 mm [THT]"]
  R5 = Resistor [tolerance=±5% resistance=100 package=THT]
  U1 = mystery part, 14 pins [chip_label="CMOS4073 (3AND)"]

nets:
  N1: Arduino1.D4, R4.Pin_0, U1.pin3
  N2: Arduino1.D3, R3.Pin_0, U1.pin4
  N3: Arduino1.D2, R1.Pin_0, U1.pin5
  N4: Arduino1.+5V, U1.pin14
  N5: Arduino1.GND, R1.Pin_1, R3.Pin_1, R4.Pin_1, R5.Pin_1, U1.pin7
  N6: LED1.cathode, U1.pin6
  N7: LED1.anode, R5.Pin_0
