# Fritzing sketch TripleAndPortCmos4073_2 (saved by Fritzing 0.8.0b)
breadboards: 1

parts:
  Arduino1 = Arduino
  R_in_3 = Resistor [tolerance=±5% resistance=10k package=THT]
  R_in_2 = Resistor [tolerance=±5% resistance=10k package=THT]
  R_in_1 = Resistor [tolerance=±5% resistance=10k package=THT]
  R_out = Resistor [tolerance=±5% resistance=100 package=THT]
  CMOS_1 = mystery part, 14 pins [chip_label="CMOS4073 (3AND)"]
  Led_out = LED - 5mm [color="Red (633nm)" package="5 mm [THT]"]

nets:
  N1: Arduino1.GND, R_in_3.Pin_0, R_in_2.Pin_0, R_in_1.Pin_0, CMOS_1.pin7, Led_out.cathode
  N2: Arduino1.D4, R_in_1.Pin_1, CMOS_1.pin3
  N3: Arduino1.D3, R_in_2.Pin_1, CMOS_1.pin4
  N4: Arduino1.D2, R_in_3.Pin_1, CMOS_1.pin5
  N5: Arduino1.+5V, CMOS_1.pin1
  N6: R_out.Pin_0, Led_out.anode
  N7: R_out.Pin_1, CMOS_1.pin6
